# Fritzing sketch DSDetector (saved by Fritzing 0.9.3b)
breadboards: 1

parts:
  Arduino_Mega_2560_(Rev3) = Arduino Mega 2560 (Rev3)
  Sensor_de_Temperatura = DS18B20 1-Wire Temperature Sensor [part_number=DS18B20]
  Botão = Square Pushbutton
  LED = LED - 5mm [color="Red (633nm)" package="5 mm [THT]"]
  R1 = Resistor [tolerance=±5% resistance=1k package=THT]

nets:
  N1: Arduino_Mega_2560_(Rev3).D13_PWM, Sensor_de_Temperatura.VDD, R1.Pin_1
  N2: Arduino_Mega_2560_(Rev3).D12_PWM, Botão.leg0
  N3: Arduino_Mega_2560_(Rev3).D11_PWM, LED.anode
  N4: Arduino_Mega_2560_(Rev3).5V, Sensor_de_Temperatura.DQ, R1.Pin_0
  GND: Arduino_Mega_2560_(Rev3).GND, Sensor_de_Temperatura.GND, Botão.leg1, LED.cathode
