# Fritzing sketch EsquematicoProjeto (saved by Fritzing 0.9.3b)
breadboards: 1

parts:
  DS1 = DS18B20 1-Wire Temperature Sensor Probe Cable
  Componente1 = Arduino Mega 2560 (Rev3)
  LED1 = LED - 5mm [color="Red (633nm)" package="5 mm [THT]"]
  R1 = Resistor [tolerance=±5% resistance=100 package=THT]
  R2 = Resistor [tolerance=±5% resistance=150 package=THT]
  R3 = Resistor [tolerance=±5% resistance=4.7k package=THT]
  S1 = Square Pushbutton
  Componente2 = LCD Keypad Shield
  Componente3 = MQ-3 breakout
  KY-1 = Keyes Relay [package=THT]
  R4 = Resistor [tolerance=±5% resistance=10k package="2512 [SMD]"]
  J1 = Piezo Speaker

nets:
  GND: DS1.GND, Componente1.GND, LED1.cathode, R2.Pin_1, Componente2.GND, Componente3.GND, KY-1.power, J1.pin1
  VDD: DS1.VDD, Componente1.5V, R3.Pin_0, S1.leg1, Componente2.+5V, Componente3.VCC, KY-1.signal
  N1: DS1.shield, Componente1.D13_PWM, R3.Pin_1
  N2: Componente1.A0, Componente2.A1
  N3: Componente1.A1, Componente3.AO, R4.Pin_0, R4.Pin_1
  N4: Componente1.D12_PWM, R2.Pin_0, S1.leg0
  N5: Componente1.D11_PWM, LED1.anode, R1.Pin_0, R1.Pin_1
  N6: Componente1.D10_PWM, KY-1.ground
  N7: Componente1.RESET, Componente2.RESET
  3V3: Componente1.3V3, Componente2.+3V3
  VIN: Componente1.VIN, Componente2.VIN
  N8: Componente1.D3_PWM, J1.pin2

notes:
  Ignição

custom parts:
  LCD Keypad Shield: It consists of a 1602 white character blue backlight LCD. The keypad consists of 5 keys — select, up, right, down and left. To save the digital IO pins, the keypad interface uses only one ADC channel. The key value is read through a 5 stage voltage divider.
  MQ-3 breakout: Alcohol sensor is capable of detecting alcohol (ethanol) particles on itself and gives the information in digital form back to us to manipulate with it. SKU:101251 • Voltage: 5V DC • Power: max 750mW • Measurement range: 0.04-4mg/L
  Keyes Relay: The Keyes 5V relay module is suitable for SCM development, home appliance control. It uses a 5V~12V TIL control signal which can control DC / AC signal.
